// Logisim project trisCircuit.circ as structural Verilog: 6 circuits, main circuit Riempi Blocco
module main (
);

  wire Accendi___Prossima_Partita_out, button_1_out, button_2_out, button_3_out, button_4_out, button_5_out,
       button_6_out, button_7_out, button_8_out, button_9_out, or_1_out, Resetta_Punteggio_out,
       tabellone_1_o_vince, tabellone_1_x_vince;
  wire [3:0] counter_1_q, counter_2_q;
  wire [5:0] display_simbolo_1_out_3, display_simbolo_1_out_4, display_simbolo_1_out_5,
       display_simbolo_1_out_6, display_simbolo_1_out_7, scritta_vincita_1_out_16, scritta_vincita_1_out_17,
       scritta_vincita_1_out_18, scritta_vincita_1_out_19, scritta_vincita_1_out_20,
       scritta_vincita_1_out_21, scritta_vincita_1_out_22, scritta_vincita_1_out_23,
       scritta_vincita_1_out_24, scritta_vincita_1_out_25, scritta_vincita_1_out_26,
       scritta_vincita_1_out_27, scritta_vincita_1_out_28, scritta_vincita_1_out_29,
       scritta_vincita_1_out_30, scritta_vincita_1_out_31, scritta_vincita_1_out_32,
       scritta_vincita_1_out_33, scritta_vincita_1_out_34, scritta_vincita_1_out_35,
       scritta_vincita_1_out_36, scritta_vincita_1_out_37, scritta_vincita_1_out_38,
       scritta_vincita_1_out_39, scritta_vincita_1_out_40, scritta_vincita_1_out_41,
       scritta_vincita_1_out_42, scritta_vincita_1_out_43, scritta_vincita_1_out_44,
       scritta_vincita_1_out_45, scritta_vincita_1_out_46, scritta_vincita_1_out_47,
       scritta_vincita_1_out_48, scritta_vincita_1_out_49, scritta_vincita_1_z1, scritta_vincita_1_z2,
       scritta_vincita_1_z3, scritta_vincita_1_z4, scritta_vincita_1_z5, scritta_vincita_1_z6,
       scritta_vincita_1_z7, scritta_vincita_1_z8, scritta_vincita_1_z9, scritta_vincita_1_z10,
       scritta_vincita_1_z11, scritta_vincita_1_z12, scritta_vincita_1_z13, scritta_vincita_1_z14,
       tabellone_1_out_13_2, tabellone_1_out_13_3, tabellone_1_out_13_4, tabellone_1_out_16_2,
       tabellone_1_out_16_3, tabellone_1_out_16_4, tabellone_1_out_17_2, tabellone_1_out_17_3,
       tabellone_1_out_17_4, tabellone_1_out_19_2, tabellone_1_out_19_3, tabellone_1_out_19_4;
  wire [11:0] tabellone_1_out_13, tabellone_1_out_16, tabellone_1_out_17, tabellone_1_out_19;
  wire [29:0] tabellone_1_out_11, tabellone_1_out_12, tabellone_1_out_15, tabellone_1_out_18,
       tabellone_1_out_21;

  Hex_Digit_Display hex_digit_display_1 (.value(counter_1_q));  // open: dp
  Counter #(.width(4), .max('hf)) counter_1 (
    .count(tabellone_1_x_vince), .Q(counter_1_q), .clk(tabellone_1_x_vince), .clr(Resetta_Punteggio_out));  // open: load, D, carry
  Button Resetta_Punteggio (.out(Resetta_Punteggio_out));
  Button button_1 (.out(button_1_out));
  Button button_2 (.out(button_2_out));
  Button button_3 (.out(button_3_out));
  Button button_4 (.out(button_4_out));
  Button button_5 (.out(button_5_out));
  Button button_6 (.out(button_6_out));
  Hex_Digit_Display hex_digit_display_2 (.value(counter_2_q));  // open: dp
  Counter #(.width(4), .max('hf)) counter_2 (
    .count(tabellone_1_o_vince), .Q(counter_2_q), .clk(tabellone_1_o_vince), .clr(Resetta_Punteggio_out));  // open: load, D, carry
  Button button_7 (.out(button_7_out));
  Button button_8 (.out(button_8_out));
  Button button_9 (.out(button_9_out));
  Button Accendi___Prossima_Partita (.out(Accendi___Prossima_Partita_out));
  DotMatrix #(.matrixrows(6)) dotmatrix_1 (
    .col0(display_simbolo_1_out_3), .col1(display_simbolo_1_out_4), .col2(display_simbolo_1_out_5),
    .col3(display_simbolo_1_out_6), .col4(display_simbolo_1_out_7));
  Display_Simbolo display_simbolo_1 (
    .o(tabellone_1_o_vince), .x(tabellone_1_x_vince), .out_3(display_simbolo_1_out_3),
    .out_4(display_simbolo_1_out_4), .out_5(display_simbolo_1_out_5), .out_6(display_simbolo_1_out_6),
    .out_7(display_simbolo_1_out_7));
  Tabellone tabellone_1 (
    .X_vince(tabellone_1_x_vince), .O_vince(tabellone_1_o_vince), ._0_0(button_2_out), ._0_1(button_1_out),
    ._0_2(button_7_out), ._1_0(button_3_out), .Accendi___Prossima_Partita(Accendi___Prossima_Partita_out),
    ._1_1(button_4_out), ._1_2(button_8_out), ._2_0(button_5_out), ._2_1(button_6_out), ._2_2(button_9_out),
    .out_11(tabellone_1_out_11), .out_12(tabellone_1_out_12),
    .out_13({tabellone_1_out_13_4, tabellone_1_out_13_3, tabellone_1_out_13_2, tabellone_1_out_13}),
    .out_15(tabellone_1_out_15),
    .out_16({tabellone_1_out_16_4, tabellone_1_out_16_3, tabellone_1_out_16_2, tabellone_1_out_16}),
    .out_17({tabellone_1_out_17_4, tabellone_1_out_17_3, tabellone_1_out_17_2, tabellone_1_out_17}),
    .out_18(tabellone_1_out_18),
    .out_19({tabellone_1_out_19_4, tabellone_1_out_19_3, tabellone_1_out_19_2, tabellone_1_out_19}),
    .out_21(tabellone_1_out_21));
  DotMatrix #(.matrixcols(16), .matrixrows(6)) dotmatrix_2 (
    .col0(scritta_vincita_1_out_16), .col1(scritta_vincita_1_z1), .col2(scritta_vincita_1_out_17),
    .col3(scritta_vincita_1_out_18), .col4(scritta_vincita_1_out_19), .col5(scritta_vincita_1_z2),
    .col6(scritta_vincita_1_z3), .col7(scritta_vincita_1_z4), .col8(scritta_vincita_1_out_20),
    .col9(scritta_vincita_1_out_21), .col10(scritta_vincita_1_out_22), .col11(scritta_vincita_1_z5),
    .col12(scritta_vincita_1_out_23), .col13(scritta_vincita_1_out_24), .col14(scritta_vincita_1_out_25),
    .col15(scritta_vincita_1_z6));
  Scritta_vincita scritta_vincita_1 (
    .Accendi(or_1_out), .out_16(scritta_vincita_1_out_16), .out_17(scritta_vincita_1_out_17),
    .out_18(scritta_vincita_1_out_18), .out_19(scritta_vincita_1_out_19), .out_20(scritta_vincita_1_out_20),
    .out_21(scritta_vincita_1_out_21), .out_22(scritta_vincita_1_out_22), .out_23(scritta_vincita_1_out_23),
    .out_24(scritta_vincita_1_out_24), .out_25(scritta_vincita_1_out_25), .out_26(scritta_vincita_1_out_26),
    .out_27(scritta_vincita_1_out_27), .out_28(scritta_vincita_1_out_28), .out_29(scritta_vincita_1_out_29),
    .out_30(scritta_vincita_1_out_30), .out_31(scritta_vincita_1_out_31), .out_32(scritta_vincita_1_out_32),
    .out_33(scritta_vincita_1_out_33), .out_34(scritta_vincita_1_out_34), .out_35(scritta_vincita_1_out_35),
    .out_36(scritta_vincita_1_out_36), .out_37(scritta_vincita_1_out_37), .out_38(scritta_vincita_1_out_38),
    .out_39(scritta_vincita_1_out_39), .out_40(scritta_vincita_1_out_40), .out_41(scritta_vincita_1_out_41),
    .out_42(scritta_vincita_1_out_42), .out_43(scritta_vincita_1_out_43), .z2(scritta_vincita_1_z2),
    .z3(scritta_vincita_1_z3), .z4(scritta_vincita_1_z4), .z5(scritta_vincita_1_z5),
    .z6(scritta_vincita_1_z6), .z14(scritta_vincita_1_z14), .z7(scritta_vincita_1_z7),
    .z8(scritta_vincita_1_z8), .z9(scritta_vincita_1_z9), .z11(scritta_vincita_1_z11),
    .z12(scritta_vincita_1_z12), .z13(scritta_vincita_1_z13), .out_44(scritta_vincita_1_out_44),
    .out_45(scritta_vincita_1_out_45), .out_46(scritta_vincita_1_out_46), .out_47(scritta_vincita_1_out_47),
    .out_48(scritta_vincita_1_out_48), .out_49(scritta_vincita_1_out_49), .z10(scritta_vincita_1_z10),
    .z1(scritta_vincita_1_z1));
  or or_1 (or_1_out, tabellone_1_o_vince, tabellone_1_x_vince);
  DotMatrix #(.matrixrows(6)) dotmatrix_3 (
    .col0(tabellone_1_out_11[29:24]), .col1(tabellone_1_out_11[23:18]), .col2(tabellone_1_out_11[17:12]),
    .col3(tabellone_1_out_11[11:6]), .col4(tabellone_1_out_11[5:0]));
  DotMatrix #(.matrixrows(6)) dotmatrix_4 (
    .col0(tabellone_1_out_15[29:24]), .col1(tabellone_1_out_15[23:18]), .col2(tabellone_1_out_15[17:12]),
    .col3(tabellone_1_out_15[11:6]), .col4(tabellone_1_out_15[5:0]));
  DotMatrix #(.matrixrows(6)) dotmatrix_5 (
    .col0(tabellone_1_out_18[29:24]), .col1(tabellone_1_out_18[23:18]), .col2(tabellone_1_out_18[17:12]),
    .col3(tabellone_1_out_18[11:6]), .col4(tabellone_1_out_18[5:0]));
  DotMatrix #(.matrixcols(32), .matrixrows(6)) dotmatrix_6 (
    .col0(scritta_vincita_1_out_26), .col1(scritta_vincita_1_out_27), .col2(scritta_vincita_1_out_28),
    .col3(scritta_vincita_1_z7), .col4(scritta_vincita_1_z8), .col5(scritta_vincita_1_z9),
    .col6(scritta_vincita_1_out_29), .col7(scritta_vincita_1_out_30), .col8(scritta_vincita_1_out_31),
    .col9(scritta_vincita_1_out_32), .col10(scritta_vincita_1_out_33), .col11(scritta_vincita_1_z10),
    .col12(scritta_vincita_1_out_34), .col13(scritta_vincita_1_z11), .col14(scritta_vincita_1_out_35),
    .col15(scritta_vincita_1_out_36), .col16(scritta_vincita_1_out_37), .col17(scritta_vincita_1_out_38),
    .col18(scritta_vincita_1_z12), .col19(scritta_vincita_1_out_39), .col20(scritta_vincita_1_out_40),
    .col21(scritta_vincita_1_out_41), .col22(scritta_vincita_1_out_42), .col23(scritta_vincita_1_z13),
    .col24(scritta_vincita_1_out_43), .col25(scritta_vincita_1_out_44), .col26(scritta_vincita_1_out_45),
    .col27(scritta_vincita_1_z14), .col28(scritta_vincita_1_out_46), .col29(scritta_vincita_1_out_47),
    .col30(scritta_vincita_1_out_48), .col31(scritta_vincita_1_out_49));
  DotMatrix #(.matrixrows(6)) dotmatrix_7 (
    .col0(tabellone_1_out_12[29:24]), .col1(tabellone_1_out_12[23:18]), .col2(tabellone_1_out_12[17:12]),
    .col3(tabellone_1_out_12[11:6]), .col4(tabellone_1_out_12[5:0]));
  DotMatrix #(.matrixrows(6)) dotmatrix_8 (
    .col0(tabellone_1_out_16_4), .col1(tabellone_1_out_16_3), .col2(tabellone_1_out_16_2),
    .col3(tabellone_1_out_16[11:6]), .col4(tabellone_1_out_16[5:0]));
  DotMatrix #(.matrixrows(6)) dotmatrix_9 (
    .col0(tabellone_1_out_19_4), .col1(tabellone_1_out_19_3), .col2(tabellone_1_out_19_2),
    .col3(tabellone_1_out_19[11:6]), .col4(tabellone_1_out_19[5:0]));
  DotMatrix #(.matrixrows(6)) dotmatrix_10 (
    .col0(tabellone_1_out_13_4), .col1(tabellone_1_out_13_3), .col2(tabellone_1_out_13_2),
    .col3(tabellone_1_out_13[11:6]), .col4(tabellone_1_out_13[5:0]));
  DotMatrix #(.matrixrows(6)) dotmatrix_11 (
    .col0(tabellone_1_out_17_4), .col1(tabellone_1_out_17_3), .col2(tabellone_1_out_17_2),
    .col3(tabellone_1_out_17[11:6]), .col4(tabellone_1_out_17[5:0]));
  DotMatrix #(.matrixrows(6)) dotmatrix_12 (
    .col0(tabellone_1_out_21[29:24]), .col1(tabellone_1_out_21[23:18]), .col2(tabellone_1_out_21[17:12]),
    .col3(tabellone_1_out_21[11:6]), .col4(tabellone_1_out_21[5:0]));

  // Notes on the sheet:
  //   X
  //   O
endmodule

module Scritta_vincita (
  input  Accendi,
  output [5:0] z1,
  output [5:0] z2,
  output [5:0] z3,
  output [5:0] z4,
  output [5:0] z5,
  output [5:0] z6,
  output [5:0] z7,
  output [5:0] z8,
  output [5:0] z9,
  output [5:0] z10,
  output [5:0] z11,
  output [5:0] z12,
  output [5:0] z13,
  output [5:0] z14,
  output [5:0] out_16,
  output [5:0] out_17,
  output [5:0] out_18,
  output [5:0] out_19,
  output [5:0] out_20,
  output [5:0] out_21,
  output [5:0] out_22,
  output [5:0] out_23,
  output [5:0] out_24,
  output [5:0] out_25,
  output [5:0] out_26,
  output [5:0] out_27,
  output [5:0] out_28,
  output [5:0] out_29,
  output [5:0] out_30,
  output [5:0] out_31,
  output [5:0] out_32,
  output [5:0] out_33,
  output [5:0] out_34,
  output [5:0] out_35,
  output [5:0] out_36,
  output [5:0] out_37,
  output [5:0] out_38,
  output [5:0] out_39,
  output [5:0] out_40,
  output [5:0] out_41,
  output [5:0] out_42,
  output [5:0] out_43,
  output [5:0] out_44,
  output [5:0] out_45,
  output [5:0] out_46,
  output [5:0] out_47,
  output [5:0] out_48,
  output [5:0] out_49
);


  assign out_16 = {2'b00, Accendi, 1'b0, {2{Accendi}}};
  assign out_17 = {3'b000, Accendi, 1'b0, Accendi};
  assign out_18 = {2'b00, {2{Accendi}}, 1'b0, Accendi};
  assign out_19 = {2'b00, Accendi, 1'b0, Accendi, 1'b0};
  assign out_20 = {6{Accendi}};
  assign out_21 = {2'b00, Accendi, 3'b000};
  assign out_22 = {2'b00, Accendi, 3'b000};
  assign out_23 = {1'b0, {5{Accendi}}};
  assign out_24 = {3'b000, Accendi, 2'b00};
  assign out_25 = {3'b000, {3{Accendi}}};
  assign out_26 = {2'b00, {4{Accendi}}};
  assign out_27 = {2'b00, {2{Accendi}}, 1'b0, Accendi};
  assign out_28 = {2'b00, {2{Accendi}}, 1'b0, Accendi};
  assign out_29 = {2'b00, {3{Accendi}}, 1'b0};
  assign out_30 = {{5{1'b0}}, Accendi};
  assign out_31 = {3'b000, {2{Accendi}}, 1'b0};
  assign out_32 = {{5{1'b0}}, Accendi};
  assign out_33 = {2'b00, {3{Accendi}}, 1'b0};
  assign out_34 = {2'b00, Accendi, 1'b0, {2{Accendi}}};
  assign out_35 = {2'b00, {4{Accendi}}};
  assign out_36 = {3'b000, Accendi, 2'b00};
  assign out_37 = {3'b000, Accendi, 2'b00};
  assign out_38 = {4'b0000, {2{Accendi}}};
  assign out_39 = {2'b00, {4{Accendi}}};
  assign out_40 = {3'b000, Accendi, 2'b00};
  assign out_41 = {3'b000, Accendi, 2'b00};
  assign out_42 = {4'b0000, {2{Accendi}}};
  assign out_43 = {2'b00, {4{Accendi}}};
  assign out_44 = {2'b00, {2{Accendi}}, 1'b0, Accendi};
  assign out_45 = {2'b00, {2{Accendi}}, 1'b0, Accendi};
  assign out_46 = {2'b00, {4{Accendi}}};
  assign out_47 = {3'b000, Accendi, 2'b00};
  assign out_48 = {3'b000, Accendi, 2'b00};
  assign out_49 = {2'b00, Accendi, 3'b000};
  assign z1 = {6{1'b0}};
  assign z2 = {6{1'b0}};
  assign z3 = {6{1'b0}};
  assign z4 = {6{1'b0}};
  assign z5 = {6{1'b0}};
  assign z6 = {6{1'b0}};
  assign z7 = {6{1'b0}};
  assign z8 = {6{1'b0}};
  assign z9 = {6{1'b0}};
  assign z10 = {6{1'b0}};
  assign z11 = {6{1'b0}};
  assign z12 = {6{1'b0}};
  assign z13 = {6{1'b0}};
  assign z14 = {6{1'b0}};
endmodule

module Display_Simbolo (
  input  o,
  input  x,
  output [5:0] out_3,
  output [5:0] out_4,
  output [5:0] out_5,
  output [5:0] out_6,
  output [5:0] out_7
);

  or or_1 (out_3[5], o, x);

  assign out_3[4:0] = {{4{o}}, out_3[5]};
  assign out_4 = {o, x, 2'b00, x, o};
  assign out_5 = {o, 1'b0, {2{x}}, 1'b0, o};
  assign out_6 = {o, x, 2'b00, x, o};
  assign out_7 = {out_3[5], {4{o}}, out_3[5]};
endmodule

module Tabellone (
  input  _0_0,
  input  _0_1,
  input  _0_2,
  input  _1_0,
  input  _1_1,
  input  _1_2,
  input  _2_0,
  input  _2_1,
  input  _2_2,
  input  Accendi___Prossima_Partita,
  output [29:0] out_11,
  output [29:0] out_12,
  output [29:0] out_13,
  output X_vince,
  output [29:0] out_15,
  output [29:0] out_16,
  output [29:0] out_17,
  output [29:0] out_18,
  output [29:0] out_19,
  output O_vince,
  output [29:0] out_21
);

  wire _0_0_t, _0_1_t, _0_2_t, _1_0_t, _1_1_t, _1_2_t, _2_0_t, _2_1_t, _2_2_t, and_1_out, and_2_out,
       and_3_out, and_4_out, and_5_out, and_6_out, and_7_out, and_8_out, and_9_out, and_10_out, and_11_out,
       and_12_out, and_13_out, and_14_out, and_15_out, and_16_out, O00, O01, O02, O10, O11, O12, O20, O21,
       O22, t_ff_1_q, X00, X01, X02, X10, X11, X12, X20, X21, X22, xor_1_out;

  Riempi_Blocco riempi_blocco_1 (
    .Input(_0_0), .Inserisci_Cerchio(xor_1_out), .Reset(Accendi___Prossima_Partita), .X(X00), .O(O00),
    .Blocco_Inserito(_0_0_t));
  Riempi_Blocco riempi_blocco_2 (
    .Input(_0_1), .Inserisci_Cerchio(xor_1_out), .Reset(Accendi___Prossima_Partita), .X(X01), .O(O01),
    .Blocco_Inserito(_0_1_t));
  Riempi_Blocco riempi_blocco_3 (
    .Input(_0_2), .Inserisci_Cerchio(xor_1_out), .Reset(Accendi___Prossima_Partita), .X(X02), .O(O02),
    .Blocco_Inserito(_0_2_t));
  Riempi_Blocco riempi_blocco_4 (
    .Input(_1_0), .Inserisci_Cerchio(xor_1_out), .Reset(Accendi___Prossima_Partita), .X(X10), .O(O10),
    .Blocco_Inserito(_1_0_t));
  Riempi_Blocco riempi_blocco_5 (
    .Input(_1_1), .Inserisci_Cerchio(xor_1_out), .Reset(Accendi___Prossima_Partita), .X(X11), .O(O11),
    .Blocco_Inserito(_1_1_t));
  Riempi_Blocco riempi_blocco_6 (
    .Input(_1_2), .Inserisci_Cerchio(xor_1_out), .Reset(Accendi___Prossima_Partita), .X(X12), .O(O12),
    .Blocco_Inserito(_1_2_t));
  Riempi_Blocco riempi_blocco_7 (
    .Input(_2_0), .Inserisci_Cerchio(xor_1_out), .Reset(Accendi___Prossima_Partita), .X(X20), .O(O20),
    .Blocco_Inserito(_2_0_t));
  Riempi_Blocco riempi_blocco_8 (
    .Input(_2_1), .Inserisci_Cerchio(xor_1_out), .Reset(Accendi___Prossima_Partita), .X(X21), .O(O21),
    .Blocco_Inserito(_2_1_t));
  Riempi_Blocco riempi_blocco_9 (
    .Input(_2_2), .Inserisci_Cerchio(xor_1_out), .Reset(Accendi___Prossima_Partita), .X(X22), .O(O22),
    .Blocco_Inserito(_2_2_t));
  T_Flip_Flop t_ff_1 (.clk(Accendi___Prossima_Partita), .T(1'b1), .Q(t_ff_1_q), .en(1'b1));  // open: Qn, preset, reset
  Display_Simbolo display_simbolo_1 (
    .o(O00), .x(X00), .out_3(out_11[5:0]), .out_4(out_11[11:6]), .out_5(out_11[17:12]),
    .out_6(out_11[23:18]), .out_7(out_11[29:24]));
  Display_Simbolo display_simbolo_2 (
    .o(O01), .x(X01), .out_3(out_12[5:0]), .out_4(out_12[11:6]), .out_5(out_12[17:12]),
    .out_6(out_12[23:18]), .out_7(out_12[29:24]));
  Display_Simbolo display_simbolo_3 (
    .o(O02), .x(X02), .out_3(out_13[5:0]), .out_4(out_13[11:6]), .out_5(out_13[17:12]),
    .out_6(out_13[23:18]), .out_7(out_13[29:24]));
  Display_Simbolo display_simbolo_4 (
    .o(O10), .x(X10), .out_3(out_15[5:0]), .out_4(out_15[11:6]), .out_5(out_15[17:12]),
    .out_6(out_15[23:18]), .out_7(out_15[29:24]));
  Display_Simbolo display_simbolo_5 (
    .o(O11), .x(X11), .out_3(out_16[5:0]), .out_4(out_16[11:6]), .out_5(out_16[17:12]),
    .out_6(out_16[23:18]), .out_7(out_16[29:24]));
  Display_Simbolo display_simbolo_6 (
    .o(O12), .x(X12), .out_3(out_17[5:0]), .out_4(out_17[11:6]), .out_5(out_17[17:12]),
    .out_6(out_17[23:18]), .out_7(out_17[29:24]));
  Display_Simbolo display_simbolo_7 (
    .o(O20), .x(X20), .out_3(out_18[5:0]), .out_4(out_18[11:6]), .out_5(out_18[17:12]),
    .out_6(out_18[23:18]), .out_7(out_18[29:24]));
  Display_Simbolo display_simbolo_8 (
    .o(O21), .x(X21), .out_3(out_19[5:0]), .out_4(out_19[11:6]), .out_5(out_19[17:12]),
    .out_6(out_19[23:18]), .out_7(out_19[29:24]));
  Display_Simbolo display_simbolo_9 (
    .o(O22), .x(X22), .out_3(out_21[5:0]), .out_4(out_21[11:6]), .out_5(out_21[17:12]),
    .out_6(out_21[23:18]), .out_7(out_21[29:24]));
  xor xor_1 (xor_1_out, t_ff_1_q, _0_0_t, _0_1_t, _0_2_t, _1_0_t, _1_1_t, _1_2_t, _2_0_t, _2_1_t, _2_2_t);
  and and_1 (and_1_out, X00, X10, X20);
  and and_2 (and_2_out, O00, O10, O20);
  and and_3 (and_3_out, X00, X01, X02);
  and and_4 (and_4_out, X00, X11, X22);
  and and_5 (and_5_out, X20, X21, X22);
  and and_6 (and_6_out, O00, O01, O02);
  and and_7 (and_7_out, O00, O11, O22);
  and and_8 (and_8_out, O20, O21, O22);
  and and_9 (and_9_out, X01, X11, X21);
  and and_10 (and_10_out, O01, O11, O21);
  and and_11 (and_11_out, X10, X11, X12);
  and and_12 (and_12_out, X02, X11, X20);
  and and_13 (and_13_out, X02, X12, X22);
  and and_14 (and_14_out, O10, O11, O12);
  and and_15 (and_15_out, O02, O11, O20);
  and and_16 (and_16_out, O02, O12, O22);
  or or_1 (X_vince, and_3_out, and_1_out, and_4_out, and_11_out, and_12_out, and_5_out, and_9_out, and_13_out);
  or or_2 (O_vince, and_6_out, and_2_out, and_7_out, and_14_out, and_15_out, and_8_out, and_10_out, and_16_out);

  // Notes on the sheet:
  //   Alterna Simbolo
endmodule

module Riempi_Blocco (
  input  Input,
  input  Inserisci_Cerchio,
  input  Reset,
  output X,
  output Blocco_Inserito,
  output O
);

  wire and_1_out, and_2_out, demultiplexer_1_out0, demultiplexer_1_out1, latch_sr_no_clock_3_nq, or_1_out;

  Demultiplexer #(.enable("false")) demultiplexer_1 (
    .out0(demultiplexer_1_out0), .out1(demultiplexer_1_out1), .in(Input), .sel(Inserisci_Cerchio));
  and and_1 (and_1_out, latch_sr_no_clock_3_nq, demultiplexer_1_out0);
  and and_2 (and_2_out, demultiplexer_1_out1, latch_sr_no_clock_3_nq);
  Latch_SR_no_clock latch_sr_no_clock_1 (.in_1(and_1_out), .in_2(Reset), .Q(X));  // open: nQ
  or or_1 (or_1_out, X, O);
  Latch_SR_no_clock latch_sr_no_clock_2 (.in_1(and_2_out), .in_2(Reset), .Q(O));  // open: nQ
  Latch_SR_no_clock latch_sr_no_clock_3 (
    .in_1(or_1_out), .in_2(Reset), .nQ(latch_sr_no_clock_3_nq), .Q(Blocco_Inserito));
endmodule

module Latch_SR_no_clock (
  input  in_1,
  input  in_2,
  output nQ,
  output Q
);

  nor nor_1 (nQ, in_1, Q);
  nor nor_2 (Q, nQ, in_2);
endmodule
